# Fritzing sketch watersensor (saved by Fritzing 0.9.2b)
breadboards: 1

parts:
  Moisture_Sensor = SparkFun Soil Moisture Sensor [part_number=SEN-13322]
  Part1 = Photon
  Water_sensor = BH1750

nets:
  VCC: Moisture_Sensor.VCC, Part1.3V3, Water_sensor.VCC
  GND: Moisture_Sensor.GND, Part1.GND, Water_sensor.GND
  N1: Moisture_Sensor.SIG, Part1.A0

custom parts:
  SparkFun Soil Moisture Sensor: The SparkFun Soil Moisture Sensor is a simple breakout for measuring the moisture in soil and similar materials.
  BH1750: Water Sensor
